// Logisim project 7 segment display.circ as structural Verilog: 1 circuit, main circuit 7SEG
module _7SEG (
  input  S3,
  input  S2,
  input  S1,
  input  S0,
  output a,
  output b,
  output c,
  output d,
  output e,
  output f,
  output g
);

  wire and_1_out, and_2_out, and_3_out, and_4_out, and_5_out, and_6_out, and_7_out, and_8_out, and_9_out,
       and_10_out, and_11_out, and_12_out, and_13_out, and_14_out, not_1_out, not_2_out, not_3_out,
       not_4_out, xnor_1_out, xnor_2_out;

  not not_1 (not_1_out, S3);
  not not_2 (not_2_out, S2);
  not not_3 (not_3_out, S1);
  not not_4 (not_4_out, S0);
  xnor xnor_1 (xnor_1_out, S2, S0);
  or u_a (a, S3, S1, xnor_1_out);
  and and_1 (and_1_out, not_2_out, not_3_out);
  and and_2 (and_2_out, not_1_out, not_2_out);
  or u_b (b, and_1_out, and_2_out, xnor_2_out);
  xnor xnor_2 (xnor_2_out, S1, S0);
  and and_3 (and_3_out, not_2_out, not_4_out);
  or u_c (c, not_3_out, S2, S0);
  and and_4 (and_4_out, S2, not_3_out, S0);
  and and_5 (and_5_out, S1, not_4_out);
  or u_d (d, and_3_out, and_4_out, and_5_out, and_7_out);
  and and_6 (and_6_out, not_2_out, not_4_out);
  and and_7 (and_7_out, not_1_out, not_2_out, S1);
  and and_8 (and_8_out, S1, not_4_out);
  or u_e (e, and_6_out, and_8_out);
  and and_9 (and_9_out, not_3_out, not_4_out);
  and and_10 (and_10_out, S2, not_3_out);
  or u_f (f, and_9_out, and_10_out, and_11_out, S3);
  and and_11 (and_11_out, S2, not_4_out);
  and and_12 (and_12_out, S2, not_3_out);
  and and_13 (and_13_out, S1, not_4_out);
  or u_g (g, S3, and_12_out, and_13_out, and_14_out);
  and and_14 (and_14_out, not_1_out, not_2_out, S1);
endmodule
