// Logisim project DATAPATH.circ as structural Verilog: 1 circuit, main circuit main
module main (
  input  A,
  input  B,
  input  C,
  input  D,
  input  E,
  input  F,
  input  G,
  input  H,
  input  I,
  input  J,
  input  K,
  input  L,
  input  M,
  input  N,
  input  O,
  input  P,
  input  Q,
  input  R,
  input  S,
  input  T,
  input  U,
  input  V,
  input  W,
  input  X,
  input  Y,
  input  Z,
  input  fail_inc,
  input  Res,
  input  Ltemp,
  input  Len,
  input  clock,
  input  i_inc,
  input  i_res,
  input  flag_init,
  input  disp_cntr,
  input  res_win,
  input  TTYRes,
  input  res_found,
  output ent,
  output [3:0] fail_cntr,
  output fail,
  output kp_cnt,
  output gr_cnt,
  output a_2,
  output b_2,
  output c_2,
  output d_2,
  output win,
  output e_2,
  output f_2,
  output l_eql,
  output [6:0] ascii,
  output g_2,
  output kp_disp,
  output wrt_en,
  output clr,
  output found
);

  wire and_1_out, and_2_out, and_3_out, and_4_out, and_5_out, and_6_out, and_7_out, and_8_out,
       decoder_1_out0, decoder_1_out1, decoder_1_out2, decoder_1_out3, decoder_1_out4, decoder_1_out5,
       decoder_1_out6, decoder_1_out7, found_q, or_1_out, or_2_out, or_3_out, register_1_q, register_2_q,
       register_3_q, register_4_q, register_5_q, register_6_q, register_7_q, register_8_q;
  wire [2:0] i_q, main_1_i_cntr;
  wire [2:2] not_1_out;
  wire [3:0] bit_extender_1_out, bit_extender_2_out, l_cntr_q;
  wire [6:0] demultiplexer_1_out0, demultiplexer_1_out1, keyboard_1_li6, L0_q, L1_q, L2_q, L3_q, L4_q, L5_q,
       L6_q, L7_q, multiplexer_1_out, temp_q;

  or or_1 (or_1_out, Res, res_found);
  Register #(.width(1)) u_found (.D(l_eql), .en(l_eql), .Q(found_q), .clk(clock), .clr(or_1_out));
  Demultiplexer #(.width(7), .enable("false")) demultiplexer_1 (
    .out0(demultiplexer_1_out0), .out1(demultiplexer_1_out1), .in(keyboard_1_li6), .sel(Len));
  Comparator #(.width(1), .mode("unsigned")) comparator_1 (.a(found_q), .b(1'b1), .eq(found));  // open: gt, lt
  Counter #(.width(3), .max('h7)) u_i (.count(i_inc), .Q(i_q), .clk(clock), .clr(or_2_out));  // open: load, D, carry
  or or_2 (or_2_out, Res, i_res);
  and and_1 (and_1_out, flag_init, decoder_1_out0);
  and and_2 (and_2_out, flag_init, decoder_1_out1);
  Register #(.width(1)) register_1 (.D(1'b1), .en(and_1_out), .Q(register_1_q), .clk(clock), .clr(Res));
  keyboard keyboard_1 (
    .Li0(keyboard_1_li6[6]), .Li1(keyboard_1_li6[5]), .Li2(keyboard_1_li6[4]), .Li3(keyboard_1_li6[3]),
    .Li4(keyboard_1_li6[2]), .Li5(keyboard_1_li6[1]), .Li6(keyboard_1_li6[0]), .A(A), .B(B), .C(C), .D(D),
    .E(E), .F(F), .G(G), .H(H), .I(I), .J(J), .K(K), .L(L), .M(M), .N(N), .O(O), .P(P), .Q(Q), .R(R), .S(S),
    .T(T), .U(U), .V(V), .W(W), .X(X), .Y(Y), .Z(Z), .en(ent));
  Register #(.width(7)) L0 (.D(demultiplexer_1_out1), .en(Len), .Q(L0_q), .clk(clock), .clr(Res));
  Register #(.width(7)) L1 (.D(L0_q), .en(Len), .Q(L1_q), .clk(clock), .clr(Res));
  Multiplexer #(.select(3), .width(7), .enable("false")) multiplexer_1 (
    .in0(L0_q), .in1(L1_q), .in2(L2_q), .in3(L3_q), .in4(L4_q), .in5(L5_q), .in6(L6_q), .in7(L7_q),
    .out(multiplexer_1_out), .sel(i_q));
  Decoder #(.select(3), .enable("false")) decoder_1 (
    .out0(decoder_1_out0), .out1(decoder_1_out1), .out2(decoder_1_out2), .out3(decoder_1_out3),
    .out4(decoder_1_out4), .out5(decoder_1_out5), .out6(decoder_1_out6), .out7(decoder_1_out7), .sel(i_q));
  and and_3 (and_3_out, flag_init, decoder_1_out2);
  Register #(.width(1)) register_2 (.D(1'b1), .en(and_2_out), .Q(register_2_q), .clk(clock), .clr(Res));
  Register #(.width(7)) L2 (.D(L1_q), .en(Len), .Q(L2_q), .clk(clock), .clr(Res));
  and and_4 (and_4_out, decoder_1_out3, flag_init);
  Register #(.width(1)) register_3 (.D(1'b1), .en(and_3_out), .Q(register_3_q), .clk(clock), .clr(Res));
  Register #(.width(1)) register_4 (.D(1'b1), .en(and_4_out), .Q(register_4_q), .clk(clock), .clr(Res));
  Register #(.width(7)) L3 (.D(L2_q), .en(Len), .Q(L3_q), .clk(clock), .clr(Res));
  Comparator #(.width(7), .mode("unsigned")) comparator_2 (
    .a(temp_q), .b(multiplexer_1_out), .eq(l_eql));  // open: gt, lt
  and and_5 (and_5_out, decoder_1_out4, flag_init);
  and and_6 (and_6_out, decoder_1_out5, flag_init);
  Register #(.width(1)) register_5 (.D(1'b1), .en(and_5_out), .Q(register_5_q), .clk(clock), .clr(Res));
  Register #(.width(7)) L4 (.D(L3_q), .en(Len), .Q(L4_q), .clk(clock), .clr(Res));
  and and_7 (and_7_out, decoder_1_out6, flag_init);
  Register #(.width(1)) register_6 (.D(1'b1), .en(and_6_out), .Q(register_6_q), .clk(clock), .clr(Res));
  Register #(.width(7)) L5 (.D(L4_q), .en(Len), .Q(L5_q), .clk(clock), .clr(Res));
  and and_8 (and_8_out, decoder_1_out7, flag_init);
  Register #(.width(1)) register_7 (.D(1'b1), .en(and_8_out), .Q(register_7_q), .clk(clock), .clr(Res));
  Register #(.width(1)) register_8 (.D(1'b1), .en(and_7_out), .Q(register_8_q), .clk(clock), .clr(Res));
  Register #(.width(7)) L6 (.D(L5_q), .en(Len), .Q(L6_q), .clk(clock), .clr(Res));
  or or_3 (or_3_out, Res, res_win);
  Register #(.width(7)) L7 (.D(L6_q), .en(Len), .Q(L7_q), .clk(clock), .clr(Res));
  TTYDisp_main main_1 (
    .i0(register_7_q), .i1(register_8_q), .i2(register_6_q), .i3(register_5_q), .i4(register_4_q),
    .i5(register_3_q), .i6(register_2_q), .i7(register_1_q), .i_inc(disp_cntr), .res(or_3_out), .l0(L6_q),
    .l1(L6_q), .l2(L5_q), .l3(L4_q), .l4(L3_q), .l5(L2_q), .l6(L1_q), .l7(L0_q), .i_cntr(main_1_i_cntr),
    .ascii(ascii), .Clock(clock), .win(win));
  Counter #(.width(4), .max('h8)) l_cntr (.count(Len), .Q(l_cntr_q), .clk(clock), .clr(Res));  // open: load, D, carry
  Register #(.width(7)) temp (.D(demultiplexer_1_out0), .en(Ltemp), .Q(temp_q), .clk(clock), .clr(Res));
  not not_1 (not_1_out[2], 1'b1);
  Counter #(.width(4), .max('hf)) u_fail_cntr (
    .count(fail_inc), .Q(fail_cntr), .clk(clock), .clr(Res));  // open: load, D, carry
  assign bit_extender_1_out = {{1{1'b0}}, main_1_i_cntr};  // Bit_Extender bit_extender_1
  or or_4 (clr, TTYRes, Res);
  Comparator #(.width(4), .mode("unsigned")) comparator_3 (
    .a(fail_cntr), .b({1'b1, not_1_out[2], 1'b1, not_1_out[2]}), .eq(fail));  // open: gt, lt
  Comparator #(.width(4), .mode("unsigned")) comparator_4 (
    .a(bit_extender_1_out), .b(l_cntr_q), .lt(kp_disp));  // open: gt, eq
  assign bit_extender_2_out = {{1{1'b0}}, i_q};  // Bit_Extender bit_extender_2
  Comparator #(.width(4), .mode("unsigned")) comparator_5 (
    .a(bit_extender_2_out), .b(l_cntr_q), .lt(kp_cnt));  // open: gt, eq
  Comparator #(.width(4), .mode("unsigned")) comparator_6 (
    .a(l_cntr_q), .b({1'b1, {3{not_1_out[2]}}}), .gt(gr_cnt));  // open: eq, lt
  _7SEG u_7seg_1 (
    .S3(l_cntr_q[3]), .S2(l_cntr_q[2]), .S1(l_cntr_q[1]), .S0(l_cntr_q[0]), .a(a_2), .b(b_2), .c(c_2),
    .d(d_2), .e(e_2), .f(f_2), .g(g_2));

  assign wrt_en = disp_cntr;

  // Notes on the sheet:
  //   i < l_cntr
  //   l_cntr > 8
endmodule
