// Logisim project Hangman.circ as structural Verilog: 1 circuit, main circuit main
module main (
  input  B,
  input  C,
  input  D,
  input  E,
  input  F,
  input  G,
  input  H,
  input  I,
  input  J,
  input  K,
  input  L,
  input  M,
  input  N,
  input  O,
  input  P,
  input  Q,
  input  R,
  input  S,
  input  T,
  input  U,
  input  V,
  input  W,
  input  X,
  input  Y,
  input  Z,
  input  enable,
  output [3:0] fail_cnt
);

  wire A_out, clock_out, enter_out, main_1_p1, main_1_p2, main_1_p3, main_1_p4, main_1_p5, main_1_p6,
       main_1_p7, main_1_p8, main_1_p13, main_1_p14, main_1_p15, main_1_p16, main_1_p17, main_1_p18,
       main_1_p19, main_1_p20, main_1_p21, main_1_p22, main_1_p23, main_2_a_2, main_2_b_2, main_2_c_2,
       main_2_clr, main_2_d_2, main_2_e_2, main_2_f_2, main_2_g_2, main_2_wrt_en, or_1_out, reset_out;
  wire [6:0] main_2_ascii;

  Button enter (.out(enter_out));
  Clock clock (.out(clock_out));
  Button reset (.out(reset_out));
  // ControlUnit_main main_1: pin names not known; wires that end beside it: main_1_p1, main_1_p2, main_1_p3, main_1_p4, main_1_p5, main_1_p6, main_1_p7, main_1_p8, enter_out, enable, clock_out, reset_out, main_1_p13, main_1_p14, main_1_p15, main_1_p16, main_1_p17, main_1_p18, main_1_p19, main_1_p20, main_1_p21, main_1_p22, main_1_p23
  Button A (.out(A_out));
  or or_1 (or_1_out, main_1_p23, reset_out);
  DATAPATH_main main_2 (
    .fail_inc(main_1_p22), .Res(or_1_out), .Ltemp(main_1_p16), .Len(main_1_p15), .clock(clock_out),
    .i_inc(main_1_p14), .i_res(main_1_p13), .flag_init(main_1_p18), .disp_cntr(main_1_p19),
    .res_win(main_1_p17), .TTYRes(main_1_p21), .res_found(main_1_p20), .A(A_out), .B(B), .C(C), .D(D), .E(E),
    .F(F), .G(G), .H(H), .I(I), .J(J), .K(K), .L(L), .M(M), .N(N), .O(O), .P(P), .Q(Q), .R(R), .S(S), .T(T),
    .U(U), .V(V), .W(W), .X(X), .Y(Y), .Z(Z), .found(main_1_p4), .ent(main_1_p1), .l_eql(main_1_p3),
    .win(main_1_p8), .fail(main_1_p7), .kp_disp(main_1_p5), .kp_cnt(main_1_p6), .gr_cnt(main_1_p2),
    .fail_cntr(fail_cnt), .a_2(main_2_a_2), .b_2(main_2_b_2), .c_2(main_2_c_2), .d_2(main_2_d_2),
    .e_2(main_2_e_2), .f_2(main_2_f_2), .ascii(main_2_ascii), .g_2(main_2_g_2), .wrt_en(main_2_wrt_en),
    .clr(main_2_clr));
  TTY tty_1 (.data(main_2_ascii), .clk(clock_out), .we(main_2_wrt_en), .clr(main_2_clr));
  _7_Segment_Display u_7_segment_display_1 (
    .g(main_2_g_2), .f(main_2_f_2), .a(main_2_a_2), .b(main_2_b_2), .e(main_2_e_2), .d(main_2_d_2),
    .c(main_2_c_2));  // open: dp

  // Notes on the sheet:
  //   NUMBER OF LETTERS
endmodule
