// Logisim project TTYDisp.circ as structural Verilog: 1 circuit, main circuit main
module main (
  input  [6:0] l0,
  input  [6:0] l1,
  input  [6:0] l2,
  input  [6:0] l3,
  input  [6:0] l4,
  input  [6:0] l5,
  input  [6:0] l6,
  input  [6:0] l7,
  input  i0,
  input  i1,
  input  i2,
  input  i3,
  input  i4,
  input  i5,
  input  i6,
  input  i7,
  input  i_inc,
  input  Clock,
  input  res,
  output [6:0] ascii,
  output [2:0] i_cntr,
  output win
);

  wire comparator_1_eq, multiplexer_1_out, multiplexer_2_out, not_2_out, not_3_out, not_4_out, or_1_out;
  wire [5:5] not_1_out;
  wire [6:0] multiplexer_3_out;

  Counter #(.width(3), .max('h7)) counter_1 (
    .count(i_inc), .Q(i_cntr), .clk(Clock), .clr(res));  // open: load, D, carry
  Multiplexer #(.select(3), .enable("false")) multiplexer_1 (
    .in0(i0), .in1(i1), .in2(i2), .in3(i3), .in4(i4), .in5(i5), .in6(i6), .in7(i7), .out(multiplexer_1_out),
    .sel(i_cntr));
  Multiplexer #(.enable("false")) multiplexer_2 (
    .in0(1'b1), .in1(multiplexer_1_out), .out(multiplexer_2_out), .sel(i_inc));
  not not_1 (not_1_out[5], 1'b1);
  Register #(.width(1)) u_win (.D(multiplexer_2_out), .en(or_1_out), .Q(win), .clk(Clock), .clr(res));
  Comparator #(.width(1)) comparator_1 (.a(multiplexer_1_out), .b(1'b1), .eq(comparator_1_eq));  // open: gt, lt
  not not_2 (not_2_out, i_inc);
  not not_3 (not_3_out, multiplexer_1_out);
  or or_1 (or_1_out, not_2_out, not_3_out);
  not not_4 (not_4_out, comparator_1_eq);
  Multiplexer #(.select(3), .width(7), .enable("false")) multiplexer_3 (
    .in0(l0), .in1(l1), .in2(l2), .in3(l3), .in4(l4), .in5(l5), .in6(l6), .in7(l7), .out(multiplexer_3_out),
    .sel(i_cntr));
  Multiplexer #(.width(7), .enable("false")) multiplexer_4 (
    .in0(multiplexer_3_out), .in1({1'b1, not_1_out[5], {5{1'b1}}}), .out(ascii), .sel(not_4_out));
endmodule
