// Logisim project keyboard.circ as structural Verilog: 1 circuit, main circuit keyboard
module keyboard (
  input  A,
  input  B,
  input  C,
  input  D,
  input  E,
  input  F,
  input  G,
  input  H,
  input  I,
  input  J,
  input  K,
  input  L,
  input  M,
  input  N,
  input  O,
  input  P,
  input  Q,
  input  R,
  input  S,
  input  T,
  input  U,
  input  V,
  input  W,
  input  X,
  input  Y,
  input  Z,
  output Li0,
  output Li1,
  output Li2,
  output Li3,
  output Li4,
  output Li5,
  output Li6,
  output en
);

  or or_1 (Li2, P, Q, R, S, T, U, V, W, X, Y, Z);
  or or_2 (Li3, H, I, J, K, L, M, N, O, X, Y, Z);
  or or_3 (Li4, D, E, F, G, L, M, N, O, T, U, V, W);
  or or_4 (Li5, B, C, F, G, J, K, N, O, R, S, V, W, Z);
  or or_5 (Li6, A, C, E, G, I, K, M, O, Q, S, U, W, Y);
  or or_6 (en, A, B, C, D, E, F, G, H, I, J, K, L, M, N, O, P, Q, R, S, T, U, V, W, X, Y, Z);

  assign Li0 = 1'b1;
  assign Li1 = 1'b1;
endmodule
